// Logisim project HW1_ALU.circ as structural Verilog: 1 circuit, main circuit main
module main (
  input  [3:0] X,
  input  [3:0] Y,
  input  zx,
  input  nx,
  input  zy,
  input  ny,
  input  f,
  input  no
);

  Hex_Digit_Display hex_digit_display_1 (.value(X));  // open: dp
  Hex_Digit_Display hex_digit_display_2 (.value(Y));  // open: dp

  // Notes on the sheet:
  //   Jackson Darling
  //   CSCI 221
endmodule
